// Logisim project matching game.circ as structural Verilog: 1 circuit, main circuit main
module main (
);

  wire acertado00, acertado01, acertado02, acertado03, acertado10, acertado11, acertado12, acertado13,
       acertado20, acertado21, acertado22, acertado23, acertado30, acertado31, acertado32, acertado33,
       and_17_out, and_18_out, and_19_out, and_20_out, and_21_out, and_22_out, and_23_out, and_24_out,
       and_25_out, and_26_out, and_27_out, and_28_out, and_29_out, and_30_out, and_31_out, and_32_out,
       and_33_out, and_34_out, and_35_out, and_36_out, and_37_out, and_38_out, and_46_out, and_47_out,
       and_48_out, and_49_out, and_58_out, and_59_out, and_60_out, and_61_out, and_66_out, and_67_out,
       and_68_out, and_69_out, and_70_out, and_71_out, and_72_out, and_73_out, check, comparator_1_eq,
       comparator_2_eq, comparator_2_gt, comparator_2_lt, comparator_3_eq, comparator_4_eq, comparator_5_eq,
       comparator_6_eq, comparator_7_eq, comparator_8_eq, comparator_9_eq, comparator_10_eq,
       comparator_11_eq, comparator_12_eq, comparator_13_eq, comparator_14_eq, comparator_15_eq,
       comparator_16_eq, comparator_17_eq, comparator_18_eq, comparator_19_eq, comparator_20_eq,
       comparator_21_eq, comparator_22_eq, comparator_23_eq, comparator_24_eq, comparator_25_eq,
       comparator_26_eq, comparator_27_eq, comparator_28_eq, comparator_29_eq, comparator_30_eq,
       comparator_31_eq, comparator_32_eq, comparator_33_eq, comparator_34_eq, comparator_35_eq,
       comparator_36_eq, comparator_37_eq, comparator_38_eq, comparator_39_eq, comparator_40_eq,
       comparator_41_eq, comparator_42_eq, comparator_43_eq, comparator_44_eq, comparator_45_eq,
       comparator_46_eq, comparator_47_eq, comparator_48_eq, comparator_49_eq, comparator_50_eq,
       comparator_51_eq, CONFIRMA, d_ff_1_q, d_ff_2_q, d_ff_3_q, EMPATE, estado0, estado1, estado2, estado3,
       jogador, JOGADOR_1, L00, L01, L02, L03, L10, L11, L12, L13, L20, L21, L22, L23, L30, L31, L32, L33,
       ligado, ligado00, ligado01, ligado02, ligado03, ligado10, ligado11, ligado12, ligado13, ligado20,
       ligado21, ligado22, ligado23, ligado30, ligado31, ligado32, ligado33, not_1_out, not_2_out, not_3_out,
       not_4_out, not_5_out, not_6_out, not_7_out, not_8_out, not_9_out, not_10_out, not_11_out, not_12_out,
       not_13_out, not_14_out, not_15_out, not_16_out, not_17_out, not_18_out, not_19_out, or_2_out,
       or_3_out, or_4_out, or_6_out, or_8_out, or_10_out, or_12_out, or_13_out, or_14_out, or_16_out,
       or_20_out, or_21_out, or_22_out, or_23_out, or_28_out, or_29_out, or_30_out, or_31_out, or_33_out,
       or_34_out, or_38_out, or_39_out, register_3_q, register_4_q, register_5_q, register_6_q, register_7_q,
       register_8_q, register_9_q, register_10_q, register_11_q, register_12_q, register_13_q, register_14_q,
       register_15_q, register_16_q, register_17_q, register_18_q, register_19_q, register_20_q,
       register_21_q, register_22_q, register_23_q, register_24_q, register_25_q, register_26_q,
       register_27_q, register_28_q, register_29_q, register_30_q, register_31_q, register_32_q,
       register_33_q, register_34_q, register_35_q, RESET, tunnel, tunnel_t, tunnel_t_t, tunnel_t_t_t,
       \VITÓRIA_JOGADOR_1 , \VITÓRIA_JOGADOR_2 ;
  wire [1:0] coluna, counter_1_q, linha, random_1_out, random_2_out, random_3_out, random_4_out;
  wire [3:0] _00, _01, _02, _03, _10, _11, _12, _13, _20, _21, _22, _23, _30, _31, _32, _33, adder_1_out,
       multiplexer_1_out, multiplexer_2_out, N00, N01, N02, N03, N10, N11, N12, N13, N20, N21, N22, N23, N30,
       N31, N32, N33, \PONTUAÇÃO_1 , \PONTUAÇÃO_2 , primeiro_num, segundo_num;

  LED led_1 (.in(\VITÓRIA_JOGADOR_1 ));
  LED led_2 (.in(JOGADOR_1));
  Hex_Digit_Display hex_digit_display_1 (.value(\PONTUAÇÃO_1 ));  // open: dp
  LED led_3 (.in(L00));
  Hex_Digit_Display hex_digit_display_2 (.value(_00));  // open: dp
  LED led_4 (.in(L10));
  Hex_Digit_Display hex_digit_display_3 (.value(_10));  // open: dp
  LED led_5 (.in(L20));
  Hex_Digit_Display hex_digit_display_4 (.value(_20));  // open: dp
  LED led_6 (.in(L30));
  Hex_Digit_Display hex_digit_display_5 (.value(_30));  // open: dp
  LED led_7 (.in(L01));
  Hex_Digit_Display hex_digit_display_6 (.value(_01));  // open: dp
  LED led_8 (.in(L11));
  Hex_Digit_Display hex_digit_display_7 (.value(_11));  // open: dp
  LED led_9 (.in(L21));
  Hex_Digit_Display hex_digit_display_8 (.value(_21));  // open: dp
  LED led_10 (.in(L31));
  Hex_Digit_Display hex_digit_display_9 (.value(_31));  // open: dp
  LED led_11 (.in(EMPATE));
  and and_1 (acertado00, check, ligado00);
  and and_2 (acertado01, check, ligado01);
  and and_3 (acertado02, check, ligado02);
  and and_4 (acertado03, check, ligado03);
  and and_5 (acertado10, check, ligado10);
  and and_6 (acertado11, check, ligado11);
  and and_7 (acertado12, check, ligado12);
  and and_8 (acertado13, check, ligado13);
  and and_9 (acertado20, check, ligado20);
  and and_10 (acertado21, check, ligado21);
  and and_11 (acertado22, check, ligado22);
  and and_12 (acertado23, check, ligado23);
  and and_13 (acertado30, check, ligado30);
  and and_14 (acertado31, check, ligado31);
  and and_15 (acertado32, check, ligado32);
  and and_16 (acertado33, check, ligado33);
  LED led_12 (.in(L02));
  Hex_Digit_Display hex_digit_display_10 (.value(_02));  // open: dp
  LED led_13 (.in(L12));
  Hex_Digit_Display hex_digit_display_11 (.value(_12));  // open: dp
  LED led_14 (.in(L22));
  Hex_Digit_Display hex_digit_display_12 (.value(_22));  // open: dp
  LED led_15 (.in(L32));
  Hex_Digit_Display hex_digit_display_13 (.value(_32));  // open: dp
  LED led_16 (.in(L03));
  Hex_Digit_Display hex_digit_display_14 (.value(_03));  // open: dp
  LED led_17 (.in(L13));
  Hex_Digit_Display hex_digit_display_15 (.value(_13));  // open: dp
  LED led_18 (.in(L23));
  Hex_Digit_Display hex_digit_display_16 (.value(_23));  // open: dp
  LED led_19 (.in(L33));
  Hex_Digit_Display hex_digit_display_17 (.value(_33));  // open: dp
  LED led_20 (.in(\VITÓRIA_JOGADOR_2 ));
  LED led_21 (.in(jogador));
  Hex_Digit_Display hex_digit_display_18 (.value(\PONTUAÇÃO_2 ));  // open: dp
  Button button_1 (.out(tunnel_t));
  Button button_2 (.out(tunnel_t_t));
  Button button_3 (.out(tunnel));
  Button button_4 (.out(CONFIRMA));
  Button button_5 (.out(tunnel_t_t_t));
  Button button_6 (.out(RESET));
  and and_17 (and_17_out, L00, ligado00);
  and and_18 (and_18_out, L01, ligado01);
  and and_19 (and_19_out, L02, ligado02);
  and and_20 (and_20_out, L03, ligado03);
  and and_21 (and_21_out, L10, ligado10);
  and and_22 (and_22_out, L11, ligado11);
  and and_23 (and_23_out, L12, ligado12);
  and and_24 (and_24_out, L13, ligado13);
  and and_25 (and_25_out, L20, ligado20);
  and and_26 (and_26_out, L21, ligado21);
  and and_27 (and_27_out, L22, ligado22);
  and and_28 (and_28_out, L23, ligado23);
  and and_29 (and_29_out, L30, ligado30);
  and and_30 (and_30_out, L31, ligado31);
  and and_31 (and_31_out, L32, ligado32);
  and and_32 (and_32_out, L33, ligado33);
  or or_1 (ligado, and_17_out, and_18_out, and_19_out, and_20_out, and_21_out, and_22_out, and_23_out, and_24_out, and_25_out, and_26_out, and_27_out, and_28_out, and_29_out, and_30_out, and_31_out, and_32_out);
  Adder #(.width(4)) adder_1 (.a(\PONTUAÇÃO_1 ), .b(\PONTUAÇÃO_2 ), .out(adder_1_out));  // open: cin, cout
  Comparator #(.width(4), .mode("unsigned")) comparator_1 (
    .a(adder_1_out), .b(4'b1000), .eq(comparator_1_eq));  // open: gt, lt
  Comparator #(.width(4), .mode("unsigned")) comparator_2 (
    .a(\PONTUAÇÃO_1 ), .b(\PONTUAÇÃO_2 ), .gt(comparator_2_gt), .eq(comparator_2_eq), .lt(comparator_2_lt));
  Multiplexer #(.select(4), .width(4), .enable("false")) multiplexer_1 (
    .in0(_00), .in1(_01), .in2(_02), .in3(_03), .in4(_10), .in5(_11), .in6(_12), .in7(_13), .in8(_20),
    .in9(_21), .in10(_22), .in11(_23), .in12(_30), .in13(_31), .in14(_32), .in15(_33),
    .out(multiplexer_1_out), .sel({linha, coluna}));
  Multiplexer #(.select(4), .width(4), .enable("false")) multiplexer_2 (
    .in0(_00), .in1(_01), .in2(_02), .in3(_03), .in4(_10), .in5(_11), .in6(_12), .in7(_13), .in8(_20),
    .in9(_21), .in10(_22), .in11(_23), .in12(_30), .in13(_31), .in14(_32), .in15(_33),
    .out(multiplexer_2_out), .sel({linha, coluna}));
  and and_33 (and_33_out, L00, not_1_out, CONFIRMA);
  and and_34 (and_34_out, L10, not_2_out, CONFIRMA);
  and and_35 (and_35_out, L20, not_3_out, CONFIRMA);
  and and_36 (and_36_out, L30, not_4_out, CONFIRMA);
  Register #(.width(4)) register_1 (
    .D(multiplexer_1_out), .Q(primeiro_num), .clk(and_37_out), .clr(RESET));  // open: en
  and and_37 (and_37_out, CONFIRMA, d_ff_1_q);
  or or_2 (or_2_out, estado1, RESET);
  Register #(.width(4)) register_2 (.D(multiplexer_2_out), .Q(segundo_num), .clk(and_38_out), .clr(RESET));  // open: en
  and and_38 (and_38_out, CONFIRMA, d_ff_2_q);
  or or_3 (or_3_out, estado2, RESET);
  Register #(.width(1)) register_3 (.D(and_33_out), .Q(register_3_q), .clk(and_33_out), .clr(or_6_out));  // open: en
  not not_1 (not_1_out, estado2);
  Register #(.width(1)) register_4 (.D(and_34_out), .Q(register_4_q), .clk(and_34_out), .clr(or_8_out));  // open: en
  not not_2 (not_2_out, estado2);
  Register #(.width(1)) register_5 (.D(and_35_out), .Q(register_5_q), .clk(and_35_out), .clr(or_10_out));  // open: en
  not not_3 (not_3_out, estado2);
  Register #(.width(1)) register_6 (.D(and_36_out), .Q(register_6_q), .clk(and_36_out), .clr(or_4_out));  // open: en
  or or_4 (or_4_out, RESET, estado3);
  not not_4 (not_4_out, estado2);
  D_Flip_Flop d_ff_1 (.clk(estado1), .D(estado1), .Q(d_ff_1_q), .reset(or_2_out));  // open: Qn, preset, en
  D_Flip_Flop d_ff_2 (.clk(estado2), .D(estado2), .Q(d_ff_2_q), .reset(or_3_out));  // open: Qn, preset, en
  and and_39 (\VITÓRIA_JOGADOR_1 , comparator_1_eq, comparator_2_gt);
  and and_40 (EMPATE, comparator_1_eq, comparator_2_eq);
  and and_41 (\VITÓRIA_JOGADOR_2 , comparator_1_eq, comparator_2_lt);
  Comparator #(.width(2)) comparator_3 (.a(linha), .b(2'b00), .eq(comparator_3_eq));  // open: gt, lt
  Comparator #(.width(2)) comparator_4 (.a(coluna), .b(2'b00), .eq(comparator_4_eq));  // open: gt, lt
  Comparator #(.width(2)) comparator_5 (.a(linha), .b(2'b01), .eq(comparator_5_eq));  // open: gt, lt
  Comparator #(.width(2)) comparator_6 (.a(coluna), .b(2'b00), .eq(comparator_6_eq));  // open: gt, lt
  Comparator #(.width(2)) comparator_7 (.a(linha), .b(2'b10), .eq(comparator_7_eq));  // open: gt, lt
  Comparator #(.width(2)) comparator_8 (.a(coluna), .b(2'b00), .eq(comparator_8_eq));  // open: gt, lt
  Comparator #(.width(2)) comparator_9 (.a(linha), .b(2'b11), .eq(comparator_9_eq));  // open: gt, lt
  Comparator #(.width(2)) comparator_10 (.a(coluna), .b(2'b00), .eq(comparator_10_eq));  // open: gt, lt
  Multiplexer #(.width(4), .enable("false")) multiplexer_3 (.in1(N00), .out(_00), .sel(ligado00));  // open: in0
  or or_5 (ligado00, register_3_q, register_7_q);
  or or_6 (or_6_out, RESET, estado3);
  Multiplexer #(.width(4), .enable("false")) multiplexer_4 (.in1(N10), .out(_10), .sel(ligado10));  // open: in0
  or or_7 (ligado10, register_4_q, register_8_q);
  or or_8 (or_8_out, RESET, estado3);
  Multiplexer #(.width(4), .enable("false")) multiplexer_5 (.in1(N20), .out(_20), .sel(ligado20));  // open: in0
  or or_9 (ligado20, register_5_q, register_9_q);
  or or_10 (or_10_out, RESET, estado3);
  Multiplexer #(.width(4), .enable("false")) multiplexer_6 (.in1(N30), .out(_30), .sel(ligado30));  // open: in0
  or or_11 (ligado30, register_6_q, register_10_q);
  and and_42 (L00, comparator_3_eq, comparator_4_eq);
  and and_43 (L10, comparator_5_eq, comparator_6_eq);
  and and_44 (L20, comparator_7_eq, comparator_8_eq);
  and and_45 (L30, comparator_9_eq, comparator_10_eq);
  Register #(.width(1)) register_7 (.D(acertado00), .Q(register_7_q), .clk(acertado00), .clr(RESET));  // open: en
  Register #(.width(1)) register_8 (.D(acertado10), .Q(register_8_q), .clk(acertado10), .clr(RESET));  // open: en
  Register #(.width(1)) register_9 (.D(acertado20), .Q(register_9_q), .clk(acertado20), .clr(RESET));  // open: en
  Register #(.width(1)) register_10 (.D(acertado30), .Q(register_10_q), .clk(acertado30), .clr(RESET));  // open: en
  and and_46 (and_46_out, L31, not_5_out, CONFIRMA);
  Comparator #(.width(2)) comparator_11 (.a(linha), .b(2'b00), .eq(comparator_11_eq));  // open: gt, lt
  Comparator #(.width(2)) comparator_12 (.a(coluna), .b(2'b01), .eq(comparator_12_eq));  // open: gt, lt
  Comparator #(.width(2)) comparator_13 (.a(linha), .b(2'b01), .eq(comparator_13_eq));  // open: gt, lt
  Comparator #(.width(2)) comparator_14 (.a(coluna), .b(2'b01), .eq(comparator_14_eq));  // open: gt, lt
  Comparator #(.width(2)) comparator_15 (.a(linha), .b(2'b10), .eq(comparator_15_eq));  // open: gt, lt
  Comparator #(.width(2)) comparator_16 (.a(coluna), .b(2'b01), .eq(comparator_16_eq));  // open: gt, lt
  Comparator #(.width(2)) comparator_17 (.a(linha), .b(2'b11), .eq(comparator_17_eq));  // open: gt, lt
  Comparator #(.width(2)) comparator_18 (.a(coluna), .b(2'b01), .eq(comparator_18_eq));  // open: gt, lt
  and and_47 (and_47_out, L01, not_6_out, CONFIRMA);
  and and_48 (and_48_out, L11, not_7_out, CONFIRMA);
  and and_49 (and_49_out, L21, not_8_out, CONFIRMA);
  not not_5 (not_5_out, estado2);
  and and_50 (L01, comparator_11_eq, comparator_12_eq);
  and and_51 (L11, comparator_13_eq, comparator_14_eq);
  and and_52 (L21, comparator_15_eq, comparator_16_eq);
  and and_53 (L31, comparator_17_eq, comparator_18_eq);
  Register #(.width(1)) register_11 (.D(and_47_out), .Q(register_11_q), .clk(and_47_out), .clr(or_16_out));  // open: en
  not not_6 (not_6_out, estado2);
  Register #(.width(1)) register_12 (.D(and_48_out), .Q(register_12_q), .clk(and_48_out), .clr(or_12_out));  // open: en
  not not_7 (not_7_out, estado2);
  or or_12 (or_12_out, RESET, estado3);
  Register #(.width(1)) register_13 (.D(and_49_out), .Q(register_13_q), .clk(and_49_out), .clr(or_13_out));  // open: en
  or or_13 (or_13_out, RESET, estado3);
  not not_8 (not_8_out, estado2);
  Register #(.width(1)) register_14 (.D(and_46_out), .Q(register_14_q), .clk(and_46_out), .clr(or_14_out));  // open: en
  or or_14 (or_14_out, RESET, estado3);
  Multiplexer #(.width(4), .enable("false")) multiplexer_7 (.in1(N01), .out(_01), .sel(ligado01));  // open: in0
  or or_15 (ligado01, register_11_q, register_15_q);
  or or_16 (or_16_out, RESET, estado3);
  Multiplexer #(.width(4), .enable("false")) multiplexer_8 (.in1(N11), .out(_11), .sel(ligado11));  // open: in0
  or or_17 (ligado11, register_12_q, register_16_q);
  Multiplexer #(.width(4), .enable("false")) multiplexer_9 (.in1(N21), .out(_21), .sel(ligado21));  // open: in0
  or or_18 (ligado21, register_13_q, register_17_q);
  Multiplexer #(.width(4), .enable("false")) multiplexer_10 (.in1(N31), .out(_31), .sel(ligado31));  // open: in0
  or or_19 (ligado31, register_14_q, register_18_q);
  Random #(.width(2), .seed(10)) random_1 (.clk(RESET), .out(random_1_out));  // open: next, clr
  Random #(.width(2)) random_2 (.clk(RESET), .out(random_2_out));  // open: next, clr
  Random #(.width(2), .seed(20)) random_3 (.clk(RESET), .out(random_3_out));  // open: next, clr
  Random #(.width(2), .seed(30)) random_4 (.clk(RESET), .out(random_4_out));  // open: next, clr
  Comparator #(.width(2)) comparator_19 (.a(linha), .b(2'b00), .eq(comparator_19_eq));  // open: gt, lt
  Comparator #(.width(2)) comparator_20 (.a(coluna), .b(2'b10), .eq(comparator_20_eq));  // open: gt, lt
  Comparator #(.width(2)) comparator_21 (.a(linha), .b(2'b01), .eq(comparator_21_eq));  // open: gt, lt
  Comparator #(.width(2)) comparator_22 (.a(coluna), .b(2'b10), .eq(comparator_22_eq));  // open: gt, lt
  Comparator #(.width(2)) comparator_23 (.a(linha), .b(2'b10), .eq(comparator_23_eq));  // open: gt, lt
  Comparator #(.width(2)) comparator_24 (.a(coluna), .b(2'b10), .eq(comparator_24_eq));  // open: gt, lt
  Comparator #(.width(2)) comparator_25 (.a(linha), .b(2'b11), .eq(comparator_25_eq));  // open: gt, lt
  Comparator #(.width(2)) comparator_26 (.a(coluna), .b(2'b10), .eq(comparator_26_eq));  // open: gt, lt
  Register #(.width(1), .trigger("falling")) register_15 (
    .D(acertado01), .Q(register_15_q), .clk(acertado01), .clr(RESET));  // open: en
  Register #(.width(1)) register_16 (.D(acertado11), .Q(register_16_q), .clk(acertado11), .clr(RESET));  // open: en
  Register #(.width(1)) register_17 (.D(acertado21), .Q(register_17_q), .clk(acertado21), .clr(RESET));  // open: en
  Register #(.width(1)) register_18 (.D(acertado31), .Q(register_18_q), .clk(acertado31), .clr(RESET));  // open: en
  and and_54 (L02, comparator_19_eq, comparator_20_eq);
  and and_55 (L12, comparator_21_eq, comparator_22_eq);
  and and_56 (L22, comparator_23_eq, comparator_24_eq);
  and and_57 (L32, comparator_25_eq, comparator_26_eq);
  and and_58 (and_58_out, L12, not_9_out, CONFIRMA);
  and and_59 (and_59_out, L22, not_10_out, CONFIRMA);
  and and_60 (and_60_out, L32, not_11_out, CONFIRMA);
  Comparator #(.width(2)) comparator_27 (.a(random_1_out), .b(2'b00), .eq(comparator_27_eq));  // open: gt, lt
  Comparator #(.width(2)) comparator_28 (.a(random_1_out), .b(2'b01), .eq(comparator_28_eq));  // open: gt, lt
  Comparator #(.width(2)) comparator_29 (.a(random_1_out), .b(2'b10), .eq(comparator_29_eq));  // open: gt, lt
  Comparator #(.width(2)) comparator_30 (.a(random_1_out), .b(2'b11), .eq(comparator_30_eq));  // open: gt, lt
  Comparator #(.width(2)) comparator_31 (.a(random_2_out), .b(2'b00), .eq(comparator_31_eq));  // open: gt, lt
  Comparator #(.width(2)) comparator_32 (.a(random_2_out), .b(2'b01), .eq(comparator_32_eq));  // open: gt, lt
  Comparator #(.width(2)) comparator_33 (.a(random_2_out), .b(2'b10), .eq(comparator_33_eq));  // open: gt, lt
  Comparator #(.width(2)) comparator_34 (.a(random_2_out), .b(2'b11), .eq(comparator_34_eq));  // open: gt, lt
  Comparator #(.width(2)) comparator_35 (.a(random_3_out), .b(2'b00), .eq(comparator_35_eq));  // open: gt, lt
  Comparator #(.width(2)) comparator_36 (.a(random_3_out), .b(2'b01), .eq(comparator_36_eq));  // open: gt, lt
  Comparator #(.width(2)) comparator_37 (.a(random_3_out), .b(2'b10), .eq(comparator_37_eq));  // open: gt, lt
  Comparator #(.width(2)) comparator_38 (.a(random_3_out), .b(2'b11), .eq(comparator_38_eq));  // open: gt, lt
  Comparator #(.width(2)) comparator_39 (.a(random_4_out), .b(2'b00), .eq(comparator_39_eq));  // open: gt, lt
  Comparator #(.width(2)) comparator_40 (.a(random_4_out), .b(2'b01), .eq(comparator_40_eq));  // open: gt, lt
  Comparator #(.width(2)) comparator_41 (.a(random_4_out), .b(2'b10), .eq(comparator_41_eq));  // open: gt, lt
  Comparator #(.width(2)) comparator_42 (.a(random_4_out), .b(2'b11), .eq(comparator_42_eq));  // open: gt, lt
  and and_61 (and_61_out, L02, not_12_out, CONFIRMA);
  not not_9 (not_9_out, estado2);
  not not_10 (not_10_out, estado2);
  not not_11 (not_11_out, estado2);
  Comparator #(.width(2)) comparator_43 (.a(linha), .b(2'b00), .eq(comparator_43_eq));  // open: gt, lt
  Comparator #(.width(2)) comparator_44 (.a(coluna), .b(2'b11), .eq(comparator_44_eq));  // open: gt, lt
  Comparator #(.width(2)) comparator_45 (.a(linha), .b(2'b01), .eq(comparator_45_eq));  // open: gt, lt
  Comparator #(.width(2)) comparator_46 (.a(coluna), .b(2'b11), .eq(comparator_46_eq));  // open: gt, lt
  Comparator #(.width(2)) comparator_47 (.a(linha), .b(2'b10), .eq(comparator_47_eq));  // open: gt, lt
  Comparator #(.width(2)) comparator_48 (.a(coluna), .b(2'b11), .eq(comparator_48_eq));  // open: gt, lt
  Comparator #(.width(2)) comparator_49 (.a(linha), .b(2'b11), .eq(comparator_49_eq));  // open: gt, lt
  Comparator #(.width(2)) comparator_50 (.a(coluna), .b(2'b11), .eq(comparator_50_eq));  // open: gt, lt
  Register #(.width(1)) register_19 (.D(and_61_out), .Q(register_19_q), .clk(and_61_out), .clr(or_20_out));  // open: en
  or or_20 (or_20_out, RESET, estado3);
  not not_12 (not_12_out, estado2);
  Register #(.width(1)) register_20 (.D(and_58_out), .Q(register_20_q), .clk(and_58_out), .clr(or_21_out));  // open: en
  or or_21 (or_21_out, RESET, estado3);
  Register #(.width(1)) register_21 (.D(and_59_out), .Q(register_21_q), .clk(and_59_out), .clr(or_22_out));  // open: en
  or or_22 (or_22_out, RESET, estado3);
  Multiplexer #(.width(4), .enable("false")) multiplexer_11 (.in1(N32), .out(_32), .sel(ligado32));  // open: in0
  Register #(.width(1)) register_22 (.D(and_60_out), .Q(register_22_q), .clk(and_60_out), .clr(or_23_out));  // open: en
  or or_23 (or_23_out, RESET, estado3);
  Multiplexer #(.width(4)) multiplexer_12 (.in1(4'b0111), .out(N00), .sel(comparator_27_eq));  // open: in0, en
  Multiplexer #(.width(4)) multiplexer_13 (.in1(4'b0101), .out(N00), .sel(comparator_28_eq));  // open: in0, en
  Multiplexer #(.width(4)) multiplexer_14 (.in1(4'b0010), .out(N00), .sel(comparator_29_eq));  // open: in0, en
  Multiplexer #(.width(4)) multiplexer_15 (.in1(4'b0001), .out(N00), .sel(comparator_30_eq));  // open: in0, en
  Multiplexer #(.width(4)) multiplexer_16 (.in1(4'b0101), .out(N10), .sel(comparator_31_eq));  // open: in0, en
  Multiplexer #(.width(4)) multiplexer_17 (.in1(4'b0011), .out(N10), .sel(comparator_32_eq));  // open: in0, en
  Multiplexer #(.width(4)) multiplexer_18 (.in1(4'b0110), .out(N10), .sel(comparator_33_eq));  // open: in0, en
  Multiplexer #(.width(4)) multiplexer_19 (.in1(4'b0011), .out(N10), .sel(comparator_34_eq));  // open: in0, en
  Multiplexer #(.width(4)) multiplexer_20 (.in1(4'b0001), .out(N20), .sel(comparator_35_eq));  // open: in0, en
  Multiplexer #(.width(4)) multiplexer_21 (.in1(4'b0100), .out(N20), .sel(comparator_36_eq));  // open: in0, en
  Multiplexer #(.width(4)) multiplexer_22 (.in1(4'b0110), .out(N20), .sel(comparator_37_eq));  // open: in0, en
  Multiplexer #(.width(4)) multiplexer_23 (.in1(4'b0111), .out(N20), .sel(comparator_38_eq));  // open: in0, en
  Multiplexer #(.width(4)) multiplexer_24 (.in1(4'b0010), .out(N30), .sel(comparator_39_eq));  // open: in0, en
  Multiplexer #(.width(4)) multiplexer_25 (.in1(4'b0000), .out(N30), .sel(comparator_40_eq));  // open: in0, en
  Multiplexer #(.width(4)) multiplexer_26 (.in1(4'b0000), .out(N30), .sel(comparator_41_eq));  // open: in0, en
  Multiplexer #(.width(4)) multiplexer_27 (.in1(4'b0100), .out(N30), .sel(comparator_42_eq));  // open: in0, en
  and and_62 (L03, comparator_43_eq, comparator_44_eq);
  and and_63 (L13, comparator_45_eq, comparator_46_eq);
  and and_64 (L23, comparator_47_eq, comparator_48_eq);
  and and_65 (L33, comparator_49_eq, comparator_50_eq);
  Multiplexer #(.width(4), .enable("false")) multiplexer_28 (.in1(N02), .out(_02), .sel(ligado02));  // open: in0
  or or_24 (ligado02, register_19_q, register_24_q);
  Multiplexer #(.width(4), .enable("false")) multiplexer_29 (.in1(N12), .out(_12), .sel(ligado12));  // open: in0
  or or_25 (ligado12, register_20_q, register_25_q);
  Multiplexer #(.width(4), .enable("false")) multiplexer_30 (.in1(N22), .out(_22), .sel(ligado22));  // open: in0
  or or_26 (ligado22, register_21_q, register_26_q);
  or or_27 (ligado32, register_22_q, register_23_q);
  Register #(.width(1)) register_23 (.D(acertado32), .Q(register_23_q), .clk(acertado32), .clr(RESET));  // open: en
  Multiplexer #(.width(4)) multiplexer_31 (.in1(4'b0010), .out(N01), .sel(comparator_27_eq));  // open: in0, en
  Multiplexer #(.width(4)) multiplexer_32 (.in1(4'b0001), .out(N01), .sel(comparator_28_eq));  // open: in0, en
  Multiplexer #(.width(4)) multiplexer_33 (.in1(4'b0111), .out(N01), .sel(comparator_29_eq));  // open: in0, en
  Multiplexer #(.width(4)) multiplexer_34 (.in1(4'b0101), .out(N01), .sel(comparator_30_eq));  // open: in0, en
  Multiplexer #(.width(4)) multiplexer_35 (.in1(4'b0011), .out(N11), .sel(comparator_31_eq));  // open: in0, en
  Multiplexer #(.width(4)) multiplexer_36 (.in1(4'b0110), .out(N11), .sel(comparator_32_eq));  // open: in0, en
  Multiplexer #(.width(4)) multiplexer_37 (.in1(4'b0011), .out(N11), .sel(comparator_33_eq));  // open: in0, en
  Multiplexer #(.width(4)) multiplexer_38 (.in1(4'b0011), .out(N11), .sel(comparator_34_eq));  // open: in0, en
  Multiplexer #(.width(4)) multiplexer_39 (.in1(4'b0100), .out(N21), .sel(comparator_35_eq));  // open: in0, en
  Multiplexer #(.width(4)) multiplexer_40 (.in1(4'b0111), .out(N21), .sel(comparator_36_eq));  // open: in0, en
  Multiplexer #(.width(4)) multiplexer_41 (.in1(4'b0001), .out(N21), .sel(comparator_37_eq));  // open: in0, en
  Multiplexer #(.width(4)) multiplexer_42 (.in1(4'b0110), .out(N21), .sel(comparator_38_eq));  // open: in0, en
  Multiplexer #(.width(4)) multiplexer_43 (.in1(4'b0000), .out(N31), .sel(comparator_39_eq));  // open: in0, en
  Multiplexer #(.width(4)) multiplexer_44 (.in1(4'b0100), .out(N31), .sel(comparator_40_eq));  // open: in0, en
  Multiplexer #(.width(4)) multiplexer_45 (.in1(4'b0010), .out(N31), .sel(comparator_41_eq));  // open: in0, en
  Multiplexer #(.width(4)) multiplexer_46 (.in1(4'b0010), .out(N31), .sel(comparator_42_eq));  // open: in0, en
  Register #(.width(1)) register_24 (.D(acertado02), .Q(register_24_q), .clk(acertado02), .clr(RESET));  // open: en
  Register #(.width(1)) register_25 (.D(acertado12), .Q(register_25_q), .clk(acertado12), .clr(RESET));  // open: en
  Register #(.width(1)) register_26 (.D(acertado22), .Q(register_26_q), .clk(acertado22), .clr(RESET));  // open: en
  and and_66 (and_66_out, L03, not_13_out, CONFIRMA);
  and and_67 (and_67_out, L13, not_14_out, CONFIRMA);
  and and_68 (and_68_out, L23, not_15_out, CONFIRMA);
  and and_69 (and_69_out, L33, not_16_out, CONFIRMA);
  Multiplexer #(.width(4)) multiplexer_47 (.in1(4'b0101), .out(N02), .sel(comparator_27_eq));  // open: in0, en
  Multiplexer #(.width(4)) multiplexer_48 (.in1(4'b0010), .out(N02), .sel(comparator_28_eq));  // open: in0, en
  Multiplexer #(.width(4)) multiplexer_49 (.in1(4'b0001), .out(N02), .sel(comparator_29_eq));  // open: in0, en
  Multiplexer #(.width(4)) multiplexer_50 (.in1(4'b0111), .out(N02), .sel(comparator_30_eq));  // open: in0, en
  Multiplexer #(.width(4)) multiplexer_51 (.in1(4'b0011), .out(N12), .sel(comparator_31_eq));  // open: in0, en
  Multiplexer #(.width(4)) multiplexer_52 (.in1(4'b0101), .out(N12), .sel(comparator_32_eq));  // open: in0, en
  Multiplexer #(.width(4)) multiplexer_53 (.in1(4'b0101), .out(N12), .sel(comparator_33_eq));  // open: in0, en
  Multiplexer #(.width(4)) multiplexer_54 (.in1(4'b0110), .out(N12), .sel(comparator_34_eq));  // open: in0, en
  Multiplexer #(.width(4)) multiplexer_55 (.in1(4'b0110), .out(N22), .sel(comparator_35_eq));  // open: in0, en
  Multiplexer #(.width(4)) multiplexer_56 (.in1(4'b0001), .out(N22), .sel(comparator_36_eq));  // open: in0, en
  Multiplexer #(.width(4)) multiplexer_57 (.in1(4'b0111), .out(N22), .sel(comparator_37_eq));  // open: in0, en
  Multiplexer #(.width(4)) multiplexer_58 (.in1(4'b0100), .out(N22), .sel(comparator_38_eq));  // open: in0, en
  Multiplexer #(.width(4)) multiplexer_59 (.in1(4'b0100), .out(N32), .sel(comparator_39_eq));  // open: in0, en
  Multiplexer #(.width(4)) multiplexer_60 (.in1(4'b0000), .out(N32), .sel(comparator_40_eq));  // open: in0, en
  Multiplexer #(.width(4)) multiplexer_61 (.in1(4'b0100), .out(N32), .sel(comparator_41_eq));  // open: in0, en
  Multiplexer #(.width(4)) multiplexer_62 (.in1(4'b0000), .out(N32), .sel(comparator_42_eq));  // open: in0, en
  Counter #(.width(2), .max('h3)) Y (.load(tunnel_t), .Q(coluna), .clk(or_28_out));  // open: D, count, carry, clr
  or or_28 (or_28_out, tunnel_t, tunnel);
  not not_13 (not_13_out, estado2);
  not not_14 (not_14_out, estado2);
  not not_15 (not_15_out, estado2);
  not not_16 (not_16_out, estado2);
  Multiplexer #(.width(4)) multiplexer_63 (.in1(4'b0001), .out(N03), .sel(comparator_27_eq));  // open: in0, en
  Multiplexer #(.width(4)) multiplexer_64 (.in1(4'b0111), .out(N03), .sel(comparator_28_eq));  // open: in0, en
  Multiplexer #(.width(4)) multiplexer_65 (.in1(4'b0101), .out(N03), .sel(comparator_29_eq));  // open: in0, en
  Multiplexer #(.width(4)) multiplexer_66 (.in1(4'b0010), .out(N03), .sel(comparator_30_eq));  // open: in0, en
  Multiplexer #(.width(4)) multiplexer_67 (.in1(4'b0110), .out(N13), .sel(comparator_31_eq));  // open: in0, en
  Multiplexer #(.width(4)) multiplexer_68 (.in1(4'b0011), .out(N13), .sel(comparator_32_eq));  // open: in0, en
  Multiplexer #(.width(4)) multiplexer_69 (.in1(4'b0011), .out(N13), .sel(comparator_33_eq));  // open: in0, en
  Multiplexer #(.width(4)) multiplexer_70 (.in1(4'b0101), .out(N13), .sel(comparator_34_eq));  // open: in0, en
  Multiplexer #(.width(4)) multiplexer_71 (.in1(4'b0111), .out(N23), .sel(comparator_35_eq));  // open: in0, en
  Multiplexer #(.width(4)) multiplexer_72 (.in1(4'b0110), .out(N23), .sel(comparator_36_eq));  // open: in0, en
  Multiplexer #(.width(4)) multiplexer_73 (.in1(4'b0100), .out(N23), .sel(comparator_37_eq));  // open: in0, en
  Multiplexer #(.width(4)) multiplexer_74 (.in1(4'b0001), .out(N23), .sel(comparator_38_eq));  // open: in0, en
  Multiplexer #(.width(4)) multiplexer_75 (.in1(4'b0000), .out(N33), .sel(comparator_39_eq));  // open: in0, en
  Multiplexer #(.width(4)) multiplexer_76 (.in1(4'b0010), .out(N33), .sel(comparator_40_eq));  // open: in0, en
  Multiplexer #(.width(4)) multiplexer_77 (.in1(4'b0000), .out(N33), .sel(comparator_41_eq));  // open: in0, en
  Multiplexer #(.width(4)) multiplexer_78 (.in1(4'b0000), .out(N33), .sel(comparator_42_eq));  // open: in0, en
  Register #(.width(1)) register_27 (.D(and_66_out), .Q(register_27_q), .clk(and_66_out), .clr(or_29_out));  // open: en
  or or_29 (or_29_out, RESET, estado3);
  Multiplexer #(.width(4), .enable("false")) multiplexer_79 (.in1(N13), .out(_13), .sel(ligado13));  // open: in0
  Register #(.width(1)) register_28 (.D(and_67_out), .Q(register_28_q), .clk(and_67_out), .clr(or_30_out));  // open: en
  or or_30 (or_30_out, RESET, estado3);
  Multiplexer #(.width(4), .enable("false")) multiplexer_80 (.in1(N23), .out(_23), .sel(ligado23));  // open: in0
  Register #(.width(1)) register_29 (.D(and_68_out), .Q(register_29_q), .clk(and_68_out), .clr(or_31_out));  // open: en
  or or_31 (or_31_out, RESET, estado3);
  Multiplexer #(.width(4), .enable("false")) multiplexer_81 (.in1(N33), .out(_33), .sel(ligado33));  // open: in0
  or or_32 (ligado33, register_30_q, register_33_q);
  Register #(.width(1)) register_30 (.D(and_69_out), .Q(register_30_q), .clk(and_69_out), .clr(or_33_out));  // open: en
  or or_33 (or_33_out, RESET, estado3);
  Counter #(.width(2), .max('h3)) Y_2 (.load(tunnel_t_t), .Q(linha), .clk(or_34_out));  // open: D, count, carry, clr
  or or_34 (or_34_out, tunnel_t_t, tunnel_t_t_t);
  Multiplexer #(.width(4), .enable("false")) multiplexer_82 (.in1(N03), .out(_03), .sel(ligado03));  // open: in0
  or or_35 (ligado03, register_27_q, register_34_q);
  or or_36 (ligado13, register_28_q, register_31_q);
  Register #(.width(1)) register_31 (.D(acertado13), .Q(register_31_q), .clk(acertado13), .clr(RESET));  // open: en
  or or_37 (ligado23, register_29_q, register_32_q);
  Register #(.width(1)) register_32 (.D(acertado23), .Q(register_32_q), .clk(acertado23), .clr(RESET));  // open: en
  Register #(.width(1)) register_33 (.D(acertado33), .Q(register_33_q), .clk(acertado33), .clr(RESET));  // open: en
  Register #(.width(1)) register_34 (.D(acertado03), .Q(register_34_q), .clk(acertado03), .clr(RESET));  // open: en
  Counter #(.width(4), .max('h8)) \pontuação1  (
    .Q(\PONTUAÇÃO_1 ), .clk(and_70_out), .clr(RESET));  // open: load, D, count, carry
  and and_70 (and_70_out, not_17_out, check);
  not not_17 (not_17_out, jogador);
  Counter #(.width(4), .max('h8)) \pontuação2  (
    .Q(\PONTUAÇÃO_2 ), .clk(and_71_out), .clr(RESET));  // open: load, D, count, carry
  and and_71 (and_71_out, jogador, check);
  and and_72 (and_72_out, d_ff_3_q, or_39_out);
  D_Flip_Flop d_ff_3 (.clk(CONFIRMA), .D(CONFIRMA), .Q(d_ff_3_q), .reset(d_ff_3_q));  // open: Qn, preset, en
  Counter #(.width(1), .max('h1)) u_jogador (
    .Q(jogador), .clk(and_73_out), .clr(RESET));  // open: load, D, count, carry
  and and_73 (and_73_out, register_35_q, not_19_out);
  Register #(.width(1)) register_35 (.D(estado3), .Q(register_35_q), .clk(estado3), .clr(estado0));  // open: en
  Comparator #(.width(4), .mode("unsigned")) comparator_51 (
    .a(primeiro_num), .b(segundo_num), .eq(comparator_51_eq));  // open: gt, lt
  or or_38 (or_38_out, RESET, estado3);
  or or_39 (or_39_out, not_18_out, estado2);
  not not_18 (not_18_out, ligado);
  not not_19 (not_19_out, check);
  and and_74 (check, comparator_51_eq, estado3);
  Counter #(.width(2), .max('h3)) counter_1 (
    .Q(counter_1_q), .clk(and_72_out), .clr(or_38_out));  // open: load, D, count, carry
  Comparator #(.width(2), .mode("unsigned")) comparator_52 (.a(counter_1_q), .b(2'b00), .eq(estado0));  // open: gt, lt
  Comparator #(.width(2), .mode("unsigned")) comparator_53 (.a(counter_1_q), .b(2'b01), .eq(estado1));  // open: gt, lt
  Comparator #(.width(2), .mode("unsigned")) comparator_54 (.a(counter_1_q), .b(2'b10), .eq(estado2));  // open: gt, lt
  Comparator #(.width(2), .mode("unsigned")) comparator_55 (.a(counter_1_q), .b(2'b11), .eq(estado3));  // open: gt, lt
  not not_20 (JOGADOR_1, jogador);

  // Other names for the same wires on the sheet: JOGADOR_2 = jogador
endmodule
